# Fritzing sketch BiltongMasterLayout (saved by Fritzing 1.0.2b)
circuit board: 8.38545cm x 6.03894cm
breadboards: 1

parts:
  CLK = ESP32-38PinWide [part_number=ESP32-38PinWide]
  FAN = Header 4 [package=molex-1x4_lock]
  Sense = Header 3 [package=molex-1x3_lock]
  IC1 = ULN2003A [package="DIP16 [THT]"]
  J1 = Power Jack [package=power_jack_slot]
  U1 = Voltage Regulator - 5V [package="TO220 [THT]"]
  MAIN_L_N_G = Header 3 [package=screwterminal-3.5mm-3_lock.007s]
  BULB_L_N_G = Header 3 [package=screwterminal-3.5mm-3_lock.007s]
  U2 = RELAY [package=relay-g5q]

nets:
  N1: CLK.3.3, Sense.3
  N2: CLK.VIN, U1.output_voltage
  N3: CLK.GPIO15, FAN.4
  N4: CLK.GPIO16, FAN.3
  N5: CLK.GPIO18, IC1.In_7
  N6: CLK.GPIO23, Sense.2
  N7: FAN.2, IC1.COM_-_Common, J1.PWR, U1.input_voltage, U2.COIL1
  N8: IC1.Out_7, U2.COIL2
  N9: MAIN_L_N_G.1, BULB_L_N_G.1
  N10: MAIN_L_N_G.2, U2.MAIN
  N11: MAIN_L_N_G.3, BULB_L_N_G.3
  N12: BULB_L_N_G.2, U2.NO

notes:
  ULN2003A
  BILTONG MAKER V1
  by YOKOMAFOODS.COM
  IN L7805CV OUT

custom parts:
  ESP32-38PinWide: Generic 38-Pin ESP32 with wide format (only access to one side of pins on a breadboard) based on Stephen Lilley's HiLetgo ESP-WROOM-32 ESP32 ESP-32S Development Board.
